// Logisim project Parte_c.circ as structural Verilog
module A (
  input  N0,
  input  N1,
  input  N2,
  input  N3,
  output f_a
);

  wire or_1_out, or_2_out, or_3_out, or_4_out;

  or or_1 (or_1_out, N3, N2, N1, ~N0);  // OR_Gate
  or or_2 (or_2_out, N3, ~N2, N1, N0);  // OR_Gate
  or or_3 (or_3_out, ~N3, N2, ~N1, ~N0);  // OR_Gate
  or or_4 (or_4_out, ~N3, ~N2, N1, ~N0);  // OR_Gate
  and and_1 (f_a, or_1_out, or_2_out, or_3_out, or_4_out);
endmodule

module Display_7seg (
  input  N3,
  input  N2,
  input  N1,
  input  N0
);

  wire a_1_f_a, b_1_f_b, c_1_f_c, d_1_f_d, e_1_f_e, f_1_f_f, g_1_f_g;

  E e_1 (.N0(N0), .N1(N1), .N2(N2), .N3(N3), .f_e(e_1_f_e));
  F f_1 (.N0(N0), .N1(N1), .N2(N2), .N3(N3), .f_f(f_1_f_f));
  G g_1 (.N0(N0), .N1(N1), .N2(N2), .N3(N3), .f_g(g_1_f_g));
  _7_Segment_Display u_7_segment_display_1 (
    .g(g_1_f_g), .f(f_1_f_f), .a(a_1_f_a), .b(b_1_f_b), .e(e_1_f_e), .d(d_1_f_d), .c(c_1_f_c));  // open: dp
  D d_1 (.N0(N0), .N1(N1), .N2(N2), .N3(N3), .f_d(d_1_f_d));
  A a_1 (.N0(N0), .N1(N1), .N2(N2), .N3(N3), .f_a(a_1_f_a));
  C c_1 (.N0(N0), .N1(N1), .N2(N2), .N3(N3), .f_c(c_1_f_c));
  B b_1 (.N0(N0), .N1(N1), .N2(N2), .N3(N3), .f_b(b_1_f_b));
endmodule

module B (
  input  N0,
  input  N1,
  input  N2,
  input  N3,
  output f_b
);

  wire or_1_out, or_2_out, or_3_out, or_4_out, or_5_out, or_6_out;

  or or_1 (or_1_out, N3, ~N2, N1, ~N0);  // OR_Gate
  or or_2 (or_2_out, N3, ~N2, ~N1, N0);  // OR_Gate
  or or_3 (or_3_out, ~N3, N2, ~N1, ~N0);  // OR_Gate
  or or_4 (or_4_out, ~N3, ~N2, N1, N0);  // OR_Gate
  or or_5 (or_5_out, ~N3, ~N2, ~N1, N0);  // OR_Gate
  or or_6 (or_6_out, ~N3, ~N2, ~N1, ~N0);  // OR_Gate
  and and_1 (f_b, or_1_out, or_2_out, or_3_out, or_4_out, or_5_out, or_6_out);
endmodule

module C (
  input  N0,
  input  N1,
  input  N2,
  input  N3,
  output f_c
);

  wire or_1_out, or_2_out, or_3_out, or_4_out;

  or or_1 (or_1_out, N3, N2, ~N1, N0);  // OR_Gate
  or or_2 (or_2_out, ~N3, ~N2, N1, N0);  // OR_Gate
  or or_3 (or_3_out, ~N3, ~N2, ~N1, N0);  // OR_Gate
  or or_4 (or_4_out, ~N3, ~N2, ~N1, ~N0);  // OR_Gate
  and and_1 (f_c, or_1_out, or_2_out, or_3_out, or_4_out);
endmodule

module D (
  input  N0,
  input  N1,
  input  N2,
  input  N3,
  output f_d
);

  wire or_1_out, or_2_out, or_3_out, or_4_out, or_5_out;

  or or_1 (or_1_out, N3, N2, N1, ~N0);  // OR_Gate
  or or_2 (or_2_out, N3, ~N2, N1, N0);  // OR_Gate
  or or_3 (or_3_out, N3, ~N2, ~N1, ~N0);  // OR_Gate
  or or_4 (or_4_out, ~N3, N2, ~N1, N0);  // OR_Gate
  or or_5 (or_5_out, ~N3, ~N2, ~N1, ~N0);  // OR_Gate
  and and_1 (f_d, or_1_out, or_2_out, or_3_out, or_4_out, or_5_out);
endmodule

module E (
  input  N0,
  input  N1,
  input  N2,
  input  N3,
  output f_e
);

  wire or_1_out, or_2_out, or_3_out, or_4_out, or_5_out, or_6_out;

  or or_1 (or_1_out, N3, N2, N1, ~N0);  // OR_Gate
  or or_2 (or_2_out, N3, N2, ~N1, ~N0);  // OR_Gate
  or or_3 (or_3_out, N3, ~N2, N1, N0);  // OR_Gate
  or or_4 (or_4_out, N3, ~N2, N1, ~N0);  // OR_Gate
  or or_5 (or_5_out, N3, ~N2, ~N1, ~N0);  // OR_Gate
  or or_6 (or_6_out, ~N3, N2, N1, ~N0);  // OR_Gate
  and and_1 (f_e, or_1_out, or_2_out, or_3_out, or_4_out, or_5_out, or_6_out);
endmodule

module F (
  input  N0,
  input  N1,
  input  N2,
  input  N3,
  output f_f
);

  wire or_1_out, or_2_out, or_3_out, or_4_out, or_5_out;

  or or_1 (or_1_out, N3, N2, N1, ~N0);  // OR_Gate
  or or_2 (or_2_out, N3, N2, ~N1, N0);  // OR_Gate
  or or_3 (or_3_out, N3, N2, ~N1, ~N0);  // OR_Gate
  or or_4 (or_4_out, N3, ~N2, ~N1, ~N0);  // OR_Gate
  or or_5 (or_5_out, ~N3, ~N2, N1, ~N0);  // OR_Gate
  and and_1 (f_f, or_1_out, or_2_out, or_3_out, or_4_out, or_5_out);
endmodule

module G (
  input  N0,
  input  N1,
  input  N2,
  input  N3,
  output f_g
);

  wire or_1_out, or_2_out, or_3_out, or_4_out;

  or or_1 (or_1_out, N3, N2, N1, N0);
  or or_2 (or_2_out, N3, N2, N1, ~N0);  // OR_Gate
  or or_3 (or_3_out, N3, ~N2, ~N1, ~N0);  // OR_Gate
  or or_4 (or_4_out, ~N3, ~N2, N1, N0);  // OR_Gate
  and and_1 (f_g, or_1_out, or_2_out, or_3_out, or_4_out);
endmodule
